# Fritzing sketch 2014春合宿_回路図案 (saved by Fritzing 0.8.5b)
breadboards: 1

parts:
  パーツ1 = Arduino Uno (Rev3)
  R1 = PHOTOCELL [package=photocell-kit]
  R2 = Resistor [tolerance=±5% resistance=220 package=THT]

nets:
  N1: パーツ1.A0, R1.P$2
  N2: パーツ1.GND, R1.P$1, R2.Pin_1
  N3: パーツ1.5V, R2.Pin_0
